# Fritzing sketch CurrenctTracker (saved by Fritzing 0.9.3b)
breadboards: 1

parts:
  Part1 = Adafruit Feather HUZZAH ESP8266 [part_number="Adafruit #2821"]
  Part2 = LCD1602-I2C
  J1 = Basic Servo
  S1 = Momentary Switch [package=ksa_sealed_tac_switch]
  LED1 = smd LED [color="Red (633nm)" package="0805 [SMD]"]
  LED2 = smd LED [color="Red (633nm)" package="0805 [SMD]"]
  LED3 = smd LED [color="Green (570nm)" package="0805 [SMD]"]
  LED4 = smd LED [color="Green (570nm)" package="0805 [SMD]"]

nets:
  GND: Part1.GND, Part2.GND, J1.gnd, S1.1, LED1.cathode, LED2.cathode, LED3.cathode, LED4.cathode
  3.3V: Part1.3.3V, J1.vcc
  N1: Part1.VBAT, Part2.VCC
  N2: Part1.GPIO14/SCK, J1.pulse
  N3: Part1.GPIO12/MISO, S1.4
  N4: Part1.GPIO13/MOSI, LED1.anode, LED2.anode
  N5: Part1.GPIO15, LED3.anode, LED4.anode
  N6: Part1.GPIO5/SCL, Part2.SCL
  N7: Part1.GPIO4/SDA, Part2.SDA

custom parts:
  Adafruit Feather HUZZAH ESP8266: his is the Adafruit Feather HUZZAH ESP8266 - our take on an 'all-in-one' ESP8266 WiFi development board with built in USB and battery charging. Its an ESP8266 WiFi module with all the extras you need, ready to rock! We have other boards in the Feather family, check'em out here. At the Feather HUZZAH's heart is an ESP8266 WiFi microcontroller clocked at 80 MHz and at 3.3V logic. This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
  LCD1602-I2C: A standard character display, usually with 2x16 characters. Comes in many colors with LCM1602 IIC attached.
